# Fritzing sketch totem_fritzing_diagram (saved by Fritzing 0.9.4)
breadboards: 2

parts:
  U1 = LCD-16X2 [package=lcd-16x2_noholes]
  R1 = Trimmer Potentiometer [maximum_resistance=10kΩ package=THT]
  SdModule1 = SdModule
  Part3 = Arduino Mega 2560 (Rev3)
  ZS-042_RTC2 = ZS-042 RTC Module
  Part6 = KY-022 Infrared Receiver Module [package="Breakout board"]
  R2 = Resistor [tolerance=±5% resistance=220 package=THT]
  J2 = GPS Module
  7LEDDiskDFR2 = 7LEDDiskDFR0106
  R3 = Resistor [tolerance=±5% resistance=220 package=THT]
  Part9 = Gravity Analog Sound Level Meter

nets:
  GND: U1.VSS, U1.R_W, U1.K, R1.leg2, SdModule1.GND, Part3.GND, ZS-042_RTC2.GND, Part6.-, J2.GND_(Black), 7LEDDiskDFR2.GRN, Part9.GND
  5V: U1.VDD, R1.leg1, SdModule1.5V, Part3.5V, ZS-042_RTC2.VCC, Part6.Vin, R2.Pin_0, J2.VCC_(Red), 7LEDDiskDFR2.5V, Part9.5V
  N1: U1.VO, R1.wiper
  N2: U1.RS, Part3.D7_PWM
  N3: U1.E, Part3.D8_PWM
  N4: U1.DB4, Part3.D9_PWM
  N5: U1.DB5, Part3.D10_PWM
  N6: U1.DB6, Part3.D11_PWM
  N7: U1.DB7, Part3.D12_PWM
  N8: U1.A, R2.Pin_1
  N9: SdModule1.SCK, Part3.D52
  N10: SdModule1.SS, Part3.D53
  N11: SdModule1.MISO, Part3.D50
  N12: SdModule1.MOSI, Part3.D51
  N13: Part3.A1, Part9.A
  N14: Part3.D21/SCL, ZS-042_RTC2.SCL
  N15: Part3.D20/SDA, ZS-042_RTC2.SDA
  N16: Part3.D19/RX1, J2.TX_(Blue)
  N17: Part3.D18/TX1, J2.RX_(Green)
  N18: Part3.D2_PWM, Part6.S
  N19: Part3.D6_PWM, R3.Pin_1
  N20: 7LEDDiskDFR2.DIN, R3.Pin_0

custom parts:
  KY-022 Infrared Receiver Module: Arduino IR receiver module KY-022, based on 1838 IR Receiver/Decoder. It reacts to 38kHz infrared light.
  Gravity Analog Sound Level Meter: In our environment, there are all kinds of sounds, some of which are quite noisy. With the development of human civilization, the quiet environments have become few and far between, and are replaced with more and more noisy environments instead. Staying in the loud places for long time will have an impact on hearing, which is bad for health. Sound level meter (also known as the decibel meter,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
